# Fritzing sketch Beepo (saved by Fritzing 0.9.3b)
circuit board: 8cm x 8cm

parts:
  LED1 = LED - 3mm [color="Green (565nm)" package="3 mm [THT]"]
  Pad1 = Pad [width=7.902222222222222 height=9.0311111111111106 connect=center]  # not connected
  Pad2 = Pad [width=7.902222222222222 height=9.0311111111111106 connect=center]  # not connected
  Pad3 = Pad [width=7.902222222222222 height=9.0311111111111106 connect=center]  # not connected
  Pad4 = Pad [width=7.902222222222222 height=9.0311111111111106 connect=center]  # not connected
  Pad5 = Pad [width=7.902222222222222 height=9.0311111111111106 connect=center]  # not connected
  Pad6 = Pad [width=7.902222222222222 height=9.0311111111111106 connect=center]  # not connected
  Pad7 = Pad [width=7.902222222222222 height=9.0311111111111106 connect=center]  # not connected
  Pad8 = Pad [width=7.902222222222222 height=9.0311111111111106 connect=center]  # not connected
  Pad9 = Pad [width=7.902222222222222 height=9.0311111111111106 connect=center]  # not connected
  Pad10 = Pad [width=7.902222222222222 height=9.0311111111111106 connect=center]  # not connected
  Pad11 = Pad [width=7.902222222222222 height=9.0311111111111106 connect=center]  # not connected
  Pad12 = Pad [width=7.902222222222222 height=9.0311111111111106 connect=center]  # not connected
  Pad13 = Pad [width=7.902222222222222 height=9.0311111111111106 connect=center]  # not connected
  Pad14 = Pad [width=7.902222222222222 height=9.0311111111111106 connect=center]  # not connected
  Pad15 = Pad [width=7.902222222222222 height=9.0311111111111106 connect=center]  # not connected
  Pad16 = Pad [width=7.902222222222222 height=9.0311111111111106 connect=center]  # not connected
  Pad17 = Pad [width=7.902222222222222 height=9.0311111111111106 connect=center]  # not connected
  Pad18 = Pad [width=7.902222222222222 height=9.0311111111111106 connect=center]  # not connected
  Pad19 = Pad [width=7.902222222222222 height=9.0311111111111106 connect=center]  # not connected
  Pad20 = Pad [width=7.902222222222222 height=9.0311111111111106 connect=center]  # not connected
  Pad21 = Pad [width=7.902222222222222 height=9.0311111111111106 connect=center]  # not connected
  Pad22 = Pad [width=7.902222222222222 height=9.0311111111111106 connect=center]  # not connected
  Pad23 = Pad [width=7.902222222222222 height=9.0311111111111106 connect=center]  # not connected
  Pad24 = Pad [width=7.902222222222222 height=9.0311111111111106 connect=center]  # not connected
  NE555 = General purpose bipolar Timer [package=dil-08]
  SPK = Piezo Speaker
  R1 = Resistor [tolerance=±5% resistance=220 package="1206 [SMD]"]
  R2 = Resistor [tolerance=±5% resistance=220 package="1206 [SMD]"]
  R3 = Resistor [tolerance=±5% resistance=220 package="1206 [SMD]"]
  R4 = Resistor [tolerance=±5% resistance=220 package="1206 [SMD]"]
  R5 = Resistor [tolerance=±5% resistance=220 package="1206 [SMD]"]
  R6 = Resistor [tolerance=±5% resistance=220 package="1206 [SMD]"]
  R7 = Resistor [tolerance=±5% resistance=220 package="1206 [SMD]"]
  R8 = Resistor [tolerance=±5% resistance=220 package="1206 [SMD]"]
  R9 = Resistor [tolerance=±5% resistance=220 package="1206 [SMD]"]
  R10 = Resistor [tolerance=±5% resistance=220 package="1206 [SMD]"]
  R11 = Resistor [tolerance=±5% resistance=220 package="1206 [SMD]"]
  R12 = Resistor [tolerance=±5% resistance=220 package="1206 [SMD]"]
  R13 = Resistor [tolerance=±5% resistance=220 package="1206 [SMD]"]
  R14 = Resistor [tolerance=±5% resistance=220 package="1206 [SMD]"]
  R15 = Resistor [tolerance=±5% resistance=220 package="1206 [SMD]"]
  R16 = Resistor [tolerance=±5% resistance=220 package="1206 [SMD]"]
  R17 = Resistor [tolerance=±5% resistance=220 package="1206 [SMD]"]
  R18 = Resistor [tolerance=±5% resistance=220 package="1206 [SMD]"]
  R19 = Resistor [tolerance=±5% resistance=220 package="1206 [SMD]"]
  R20 = Resistor [tolerance=±5% resistance=220 package="1206 [SMD]"]
  R21 = Resistor [tolerance=±5% resistance=220 package="1206 [SMD]"]
  R22 = Resistor [tolerance=±5% resistance=220 package="1206 [SMD]"]
  R23 = Resistor [tolerance=±5% resistance=220 package="1206 [SMD]"]
  R24 = Resistor [tolerance=±0.05% resistance=1k package="1206 [SMD]"]
  POT = Trimmer Potentiometer [maximum_resistance=10kΩ package=THT]
  J1 = female pin header, 1 pin [form="♀ (female)"]
  C1 = Electrolytic Capacitor [capacitance=10µF package="0605 [SMD, electrolytic]"]
  R25 = Resistor [tolerance=±5% resistance=220 package="1206 [SMD]"]
  9V = Battery block 9V
  R26 = Resistor [tolerance=±5% resistance=220 package="1206 [SMD]"]

nets:
  N1: LED1.cathode, NE555.GND, SPK.pin1, 9V.-
  N2: LED1.anode, R25.Pin_0
  N3: NE555.TRI, NE555.TRE, J1.pin1
  N4: NE555.OUT, C1.+
  N5: NE555._RES, NE555.VCC+, R25.Pin_1, 9V.+, R26.Pin_1
  N6: NE555.DIS, POT.leg1, POT.wiper, R26.Pin_0
  N7: SPK.pin2, C1.-
  N8: R1.Pin_0, POT.leg2
  N9: R1.Pin_1, R2.Pin_0
  N10: R2.Pin_1, R3.Pin_0
  N11: R3.Pin_1, R4.Pin_0
  N12: R4.Pin_1, R5.Pin_0
  N13: R5.Pin_1, R6.Pin_0
  N14: R6.Pin_1, R12.Pin_0
  N15: R7.Pin_0, R9.Pin_1
  N16: R7.Pin_1, R11.Pin_0
  N17: R8.Pin_0, R10.Pin_1
  N18: R8.Pin_1, R9.Pin_0
  N19: R10.Pin_0, R12.Pin_1
  N20: R11.Pin_1, R18.Pin_0
  N21: R13.Pin_0, R15.Pin_1
  N22: R13.Pin_1, R17.Pin_0
  N23: R14.Pin_0, R16.Pin_1
  N24: R14.Pin_1, R15.Pin_0
  N25: R16.Pin_0, R18.Pin_1
  N26: R17.Pin_1, R24.Pin_0
  N27: R19.Pin_0, R21.Pin_1
  N28: R19.Pin_1, R23.Pin_0
  N29: R20.Pin_0, R22.Pin_1
  N30: R20.Pin_1, R21.Pin_0
  N31: R22.Pin_0, R24.Pin_1
