# Fritzing sketch BlinkRelayEr (saved by Fritzing 0.9.3b)
circuit board: 8cm x 8cm

parts:
  LED1 = LED - 3mm [color="Green (565nm)" package="3 mm [THT]"]
  Relay_Coil = female pin header, 2 pins [form="♀ (female)"]
  Relay_Switch = female pin header, 3 pins [form="♀ (female)"]
  R1 = Resistor [tolerance=±5% resistance=220 package=THT]
  R2 = Resistor [tolerance=±5% resistance=220 package=THT]
  C1 = Electrolytic Capacitor [capacitance=1µF package="100 mil [THT, electrolytic]"]
  S1 = Pushbutton [package="[THT]"]
  9V = Battery block 9V

nets:
  N1: LED1.cathode, Relay_Coil.pin2, C1.-, 9V.-
  N2: LED1.anode, R1.Pin_1
  N3: Relay_Coil.pin1, R2.Pin_0, C1.+
  N4: Relay_Switch.pin1, R1.Pin_0
  N5: Relay_Switch.pin2, S1.Pin_1, S1.Pin_2
  N6: Relay_Switch.pin3, R2.Pin_1
  N7: S1.Pin_3, S1.Pin_4, 9V.+

notes:
  +
  -
  NO
  NC
