# Fritzing sketch LearnAscii (saved by Fritzing 0.9.3b)
circuit board: 8cm x 8cm

parts:
  LCD1 = LCD screen
  S1 = Toggle Switch [package=THT]
  S2 = Toggle Switch [package=THT]
  S3 = Toggle Switch [package=THT]
  S4 = Toggle Switch [package=THT]
  S5 = Toggle Switch [package=THT]
  S6 = Toggle Switch [package=THT]
  S7 = Toggle Switch [package=THT]
  S8 = Toggle Switch [package=THT]
  RS = Toggle Switch [package=THT]
  R1 = Trimmer Potentiometer [maximum_resistance=10kΩ package=THT]
  S9 = Pushbutton [package="[THT]"]
  VCC1 = 4 x AAA Battery Mount
  PWR = Toggle Switch [package=THT]
  LED1 = smd LED [color="Red (633nm)" package="0603 [SMD]"]
  R1_2 = Resistor [tolerance=±5% resistance=220 package="0603 [SMD]"]

nets:
  N1: LCD1.VSS, LCD1.RS, LCD1.R/W, LCD1.LED-, RS.COM, R1.leg1, VCC1.-, LED1.cathode
  N2: LCD1.VDD, LCD1.LED+, S1.COM, S2.COM, S3.COM, S4.COM, S5.COM, S6.COM, S7.COM, S8.COM, RS.L1, R1.leg2, S9.Pin_3, S9.Pin_4, PWR.COM, R1_2.Pin_1
  N3: LCD1.V0, R1.wiper
  N4: LCD1.E, S9.Pin_2
  N5: LCD1.DB0, S1.L2
  N6: LCD1.DB1, S2.L2
  N7: LCD1.DB2, S3.L2
  N8: LCD1.DB3, S4.L2
  N9: LCD1.DB4, S5.L2
  N10: LCD1.DB5, S6.L2
  N11: LCD1.DB6, S7.L2
  N12: LCD1.DB7, S8.L2
  N13: VCC1.+, PWR.L1
  N14: LED1.anode, R1_2.Pin_0
