# Fritzing sketch LearnAscii (saved by Fritzing 0.9.3b)
circuit board: 8cm x 8cm

parts:
  LCD1 = LCD screen
  S1 = Toggle Switch [package=THT]
  S2 = Toggle Switch [package=THT]
  S3 = Toggle Switch [package=THT]
  S4 = Toggle Switch [package=THT]
  S5 = Toggle Switch [package=THT]
  S6 = Toggle Switch [package=THT]
  S7 = Toggle Switch [package=THT]
  S8 = Toggle Switch [package=THT]
  RS = Toggle Switch [package=THT]
  R1 = Trimmer Potentiometer [maximum_resistance=10kΩ package=THT]
  SEND = Pushbutton [package="[THT]"]
  PWR = Toggle Switch [package=THT]
  LED1 = smd LED [color="Red (633nm)" package="0603 [SMD]"]
  R1_2 = Resistor [tolerance=±5% resistance=220 package="0603 [SMD]"]
  VCC1 = 4 x AAA Battery Mount
  R2 = Resistor [tolerance=±5% resistance=10k package=THT]
  C1 = Electrolytic Capacitor [capacitance=1µF package="100 mil [THT, electrolytic]"]

nets:
  N1: LCD1.VSS, LCD1.RS, LCD1.R/W, LCD1.LED-, S1.L2, S2.L2, S3.L2, S4.L2, S5.L2, S6.L2, S7.L2, S8.L2, RS.COM, RS.L2, R1.leg1, LED1.cathode, VCC1.-, R2.Pin_0, C1.-
  N2: LCD1.VDD, LCD1.LED+, S1.L1, S2.L1, S3.L1, S4.L1, S5.L1, S6.L1, S7.L1, S8.L1, RS.L1, R1.leg2, SEND.Pin_3, SEND.Pin_4, PWR.COM, R1_2.Pin_1
  N3: LCD1.V0, R1.wiper
  N4: LCD1.E, SEND.Pin_1, SEND.Pin_2, R2.Pin_1, C1.+
  N5: LCD1.DB0, S1.COM
  N6: LCD1.DB1, S2.COM
  N7: LCD1.DB2, S3.COM
  N8: LCD1.DB3, S4.COM
  N9: LCD1.DB4, S5.COM
  N10: LCD1.DB5, S6.COM
  N11: LCD1.DB6, S7.COM
  N12: LCD1.DB7, S8.COM
  N13: PWR.L1, VCC1.+
  N14: LED1.anode, R1_2.Pin_0

notes:
  0
  1
  INS
  TXT
  INIT: INS00001111E
  INS00110000E
  TEXT: Standard ASCII
