# Fritzing sketch LedRocket (saved by Fritzing 0.9.3b)
circuit board: 8.00001cm x 8.00001cm

parts:
  LED1 = LED - 3mm [color="Green (555nm)" package="3 mm [THT]"]
  LED2 = LED - 3mm [color="Green (555nm)" package="3 mm [THT]"]
  LED3 = LED - 3mm [color="Green (555nm)" package="3 mm [THT]"]
  LED4 = LED - 3mm [color="Green (555nm)" package="3 mm [THT]"]
  LED5 = LED - 3mm [color="Green (555nm)" package="3 mm [THT]"]
  LED6 = LED - 3mm [color="Green (555nm)" package="3 mm [THT]"]
  LED7 = LED - 3mm [color="Green (555nm)" package="3 mm [THT]"]
  LED8 = LED - 3mm [color="Green (555nm)" package="3 mm [THT]"]
  LED9 = LED - 3mm [color="Green (555nm)" package="3 mm [THT]"]
  LED10 = smd LED [color="Red (633nm)" package="0603 [SMD]"]
  LED11 = smd LED [color="Red (633nm)" package="0603 [SMD]"]
  LED12 = smd LED [color="Orange (620nm)" package="0603 [SMD]"]
  LED13 = smd LED [color="Orange (620nm)" package="0603 [SMD]"]
  LED14 = smd LED [color="Orange (620nm)" package="0603 [SMD]"]
  LED15 = smd LED [color="Orange (620nm)" package="0603 [SMD]"]
  LED17 = smd LED [color="Orange (620nm)" package="0603 [SMD]"]
  LED18 = smd LED [color="Orange (620nm)" package="0603 [SMD]"]
  U1 = ATmega328 [package=tqfp]
  XTAL1 = Crystal [frequency="16 MHz" package=SMD]
  USB = Mini-USB _B_ connector with 5th pin broken out. [package=usb-micro_b]
  ACCU1 = Battery Holders [package=battcon_20mm]
  LED16 = smd LED [color="Orange (620nm)" package="0603 [SMD]"]
  BAT/USB = SPST Switch [package=switch-spdt-smd]
  S1 = Pushbutton [package="[SMD]"]
  ICSP = double row smd male pin header, 6 pins [form="♂ (male)"]

nets:
  GND: LED1.cathode, LED2.cathode, LED3.cathode, LED4.cathode, LED5.cathode, LED6.cathode, LED7.cathode, LED8.cathode, LED9.cathode, LED10.cathode, LED11.cathode, LED12.cathode, LED13.cathode, LED14.cathode, LED15.cathode, LED17.cathode, LED18.cathode, U1.GND, USB.GND, ACCU1.-, LED16.cathode, S1.Pin_1, S1.Pin_2, ICSP.pin6
  N1: LED1.anode, U1.PD2(INT0)
  N2: LED2.anode, U1.PD5(T1)
  N3: LED3.anode, U1.PB1(OC1A)
  N4: LED4.anode, U1.PD3(INT1)
  N5: LED5.anode, U1.PD7(AIN1)
  N6: LED6.anode, U1.PB0(ICP)
  N7: LED7.anode, U1.PD6(AIN0)
  N8: LED8.anode, U1.PB2(SS_OC1B)
  N9: LED9.anode, U1.PD4(XCK_T0)
  N10: LED10.anode, U1.PC0(ADC0)
  N11: LED11.anode, U1.PC1(ADC1)
  N12: LED12.anode, LED15.anode, U1.PC2(ADC2)
  N13: LED13.anode, U1.PC3(ADC3), LED16.anode
  N14: LED14.anode, LED17.anode, U1.PC4(ADC4_SDA)
  N15: LED18.anode, U1.PC5(ADC5_SCL)
  N16: U1.VCC, BAT/USB.S, ICSP.pin2
  N17: U1.PB6(XTAL1_TOSC1), XTAL1.pin_1
  N18: U1.PB7(XTAL2_TOSC2), XTAL1.pin_0
  N19: U1.PB3(MOSI_OC2), ICSP.pin1
  N20: U1.PB4(MISO), ICSP.pin4
  N21: U1.PB5(SCK), ICSP.pin3
  N22: U1.PC6(_RESET), S1.Pin_3, S1.Pin_4, ICSP.pin5
  N23: USB.VBUS, BAT/USB.P
  N24: ACCU1.+, BAT/USB.O
