# Fritzing sketch Shifter (saved by Fritzing 0.9.3b)
circuit board: 8cm x 8cm

parts:
  U1 = 74HC595 [package="DIP16 [THT]"]
  VCC1 = 4 x AAA Battery Mount
  S1 = Toggle Switch [package=THT]
  D1 = LED_BARGRAPH_10 [package=led_bargaph_10]
  SERIAL = Pushbutton [package="[THT]"]
  LATCH = Pushbutton [package="[THT]"]
  CLOCK = Pushbutton [package="[THT]"]
  R1 = Resistor [tolerance=±5% resistance=220 package=THT]
  LED1 = LED - 3mm [color="Green (565nm)" package="3 mm [THT]"]
  R2 = Resistor [tolerance=±5% resistance=220 package=THT]

nets:
  N1: U1.Q1, D1.C_A
  N2: U1.Q2, D1.D_A
  N3: U1.Q3, D1.E_A
  N4: U1.Q4, D1.F_A
  N5: U1.Q5, D1.G_A
  N6: U1.Q6, D1.H_A
  N7: U1.Q7, D1.I_A
  N8: U1.GND, U1.OE, VCC1.-, D1.J_C, D1.I_C, D1.H_C, D1.G_C, D1.F_C, D1.E_C, D1.D_C, D1.C_C, D1.B_C, D1.A_C, LED1.anode
  N9: U1.MR, U1.VCC, S1.L1, SERIAL.Pin_3, SERIAL.Pin_4, LATCH.Pin_3, LATCH.Pin_4, CLOCK.Pin_3, CLOCK.Pin_4, R1.Pin_1, R2.Pin_1
  N10: U1.SH_CP, CLOCK.Pin_2
  N11: U1.ST_CP, LATCH.Pin_1, LATCH.Pin_2
  N12: U1.DS, SERIAL.Pin_1, SERIAL.Pin_2
  N13: U1.Q0, D1.B_A
  N14: VCC1.+, S1.COM
  N15: D1.A_A, D1.J_A, R1.Pin_0
  N16: LED1.cathode, R2.Pin_0
